# Fritzing sketch variometer (saved by Fritzing 0.9.2b)
stripboards: 1

parts:
  Part1 = Arduino Nano (Rev3.0)
  IC1 = '4050 Hex Buffer
  Part2 = U-Blox Neo6M  # not connected
  S1 = Toggle Switch [package=THT]
  Part3 = DROTEK IMU 10DOF - MPU9250 + MS5611  # not connected
  J1 = Piezo Speaker
  R1 = Resistor [tolerance=±5% resistance=220 package="0402 [SMD]"]
  Part5 = SDcard reader
  U1 = LIPO-1000mAh [package=lipo-1000]
  Part7 = Power Cell LiPo Charger/Booster
  Part6 = n5110

nets:
  GND: Part1.GND, Part1.D11/MOSI, IC1.VSS, IC1.E, Part5.MOSI, Part5.GND, U1.+, Part7.GND, Part6.GND
  N1: Part1.D2, IC1.C
  N2: Part1.D4, IC1.B
  N3: Part1.D6, IC1.A
  N4: Part1.D8, Part5.CS
  N5: Part1.D9, J1.pin1
  N6: Part1.D10, R1.Pin_1
  N7: Part1.D12/MISO, IC1.I, Part5.MISO, Part6.CS
  5V: Part1.5V, S1.COM, S1.L2, Part7.VCC
  VCC: Part1.3V3, IC1.VCC, IC1.H, J1.pin2, R1.Pin_0, Part5.3V, Part6.LED, Part6.RST, Part6.VCC
  N8: Part1.D13/SCK, IC1.G, IC1.F, Part5.SCK, Part6.DC
  N9: IC1.K, Part6.MOSI
  N10: IC1.L, Part6.CLK
  N11: U1.-, Part7.5VIN

custom parts:
  U-Blox Neo6M: U-Blox Neo6M GPS
  Power Cell LiPo Charger/Booster: The PowerCell board is a single cell LiPo boost converter (to 3.3V and 5V) and micro-USB charger in one. The board comes with a JST connector for a single cell LiPo battery, a micro-USB connector for the 5V charge input, and selectable 3.3V and 5V output pins (labeled ‘out’). There are also two charge pins broken out (labeled ‘charge’), so you can use another 5V power source to charge the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
